# Fritzing sketch relay (saved by Fritzing 0.9.3b)
breadboards: 2

parts:
  U1 = NodeMCU V3.0
  LED1 = LED - 5mm [color="Red (633nm)" package="5 mm [THT]"]
  U2 = NodeMCU V3.0
  KY-1 = Keyes Relay [package=THT]
  LED2 = LED - 5mm [color="Green (555nm)" package="5 mm [THT]"]
  J1 = Generic female header - 3 pins [form="♀ (female)" package=THT]
  Fonte_220V = Battery
  KY-2 = Keyes Relay [package=THT]
  BULB1 = Incandescent light bulb small [package="bulb sm"]
  Fonte_5v = Battery

nets:
  N1: U1.GND, LED1.cathode, LED2.cathode
  N2: U1.D5, LED1.anode
  N3: U1.D6, LED2.anode
  N4: U2.GND, KY-1.signal, KY-2.signal, Fonte_5v.-
  N5: U2.D5, KY-2.power
  N6: U2.D6, KY-1.power
  N7: U2.Vin, KY-1.ground, KY-2.ground, Fonte_5v.+
  N8: KY-1.NC, J1.VCC
  N9: KY-1.C, Fonte_220V.+, KY-2.C
  N10: J1.GND, Fonte_220V.-, BULB1.2
  N11: KY-2.NC, BULB1.1

custom parts:
  NodeMCU V3.0: NodeMcu V3 Lua WIFI Development Board
  Keyes Relay: The Keyes 5V relay module is suitable for SCM development, home appliance control. It uses a 5V~12V TIL control signal which can control DC / AC signal.
  Generic female header - 3 pins: Generic female header
  Battery: Your standard 2x 18650 battery pack (7,4 Volts)
